// Logisim project ALU.circ as structural Verilog: 1 circuit, main circuit main
module main (
  input  [3:0] A,
  input  [3:0] B,
  input  CIN,
  output [3:0] C,
  output out_5
);

  Adder #(.width(4)) adder_1 (.a(A), .b(B), .out(C), .cin(CIN), .cout(out_5));
endmodule
